// Logisim project branch_comp.circ as structural Verilog: 1 circuit, main circuit branch_comp
module branch_comp (
  input  [31:0] rs1,
  input  [31:0] rs2,
  input  BrUn,
  output BrEq,
  output BrLt
);

  wire signed_eq, signed_lt, unsigned_eq, unsigned_lt;

  Multiplexer #(.enable("false")) multiplexer_1 (.in0(signed_eq), .in1(unsigned_eq), .out(BrEq), .sel(BrUn));
  Comparator #(.width(32)) comparator_1 (.a(rs1), .b(rs2), .eq(signed_eq), .lt(signed_lt));  // open: gt
  Comparator #(.width(32), .mode("unsigned")) comparator_2 (
    .a(rs1), .b(rs2), .eq(unsigned_eq), .lt(unsigned_lt));  // open: gt
  Multiplexer #(.enable("false")) multiplexer_2 (.in0(signed_lt), .in1(unsigned_lt), .out(BrLt), .sel(BrUn));

  // Notes on the sheet:
  //   INPUTS to your circuit
  //   signed comparator
  //   unsigned comparator
  //   DON'T CHANGE THE LOCATIONS OF THE INPUTS AND OUTPUTS!
  //   OUTPUT from your circuit
endmodule
