// Logisim project control_logic.circ as structural Verilog: 1 circuit, main circuit control_logic
module control_logic (
  input  [31:0] inst,
  input  BrEq,
  input  BrLt,
  output PCSel,
  output RegWEn,
  output [2:0] ImmSel,
  output BrUn,
  output ASel,
  output BSel,
  output [3:0] ALUSel,
  output MemRW,
  output [1:0] WBSel
);

  wire and_5_out, and_6_out, and_7_out, and_8_out, and_9_out, and_10_out, comparator_1_eq, comparator_2_eq,
       comparator_3_eq, comparator_4_eq, comparator_5_eq, comparator_6_eq, comparator_7_eq, comparator_8_eq,
       comparator_9_eq, comparator_10_eq, comparator_11_eq, comparator_12_eq, comparator_13_eq,
       comparator_14_eq, comparator_15_eq, comparator_16_eq, comparator_17_eq, comparator_18_eq,
       comparator_19_eq, comparator_20_eq, comparator_21_eq, comparator_22_eq, comparator_23_eq,
       comparator_24_eq, comparator_25_eq, comparator_26_eq, comparator_27_eq, comparator_28_eq,
       comparator_29_eq, comparator_30_eq, comparator_31_eq, comparator_32_eq, comparator_33_eq,
       comparator_34_eq, comparator_35_eq, comparator_36_eq, comparator_37_eq, comparator_38_eq,
       comparator_39_eq, comparator_40_eq, comparator_41_eq, comparator_42_eq, comparator_43_eq,
       comparator_44_eq, comparator_46_eq, comparator_47_eq, comparator_48_eq, comparator_49_eq,
       comparator_50_eq, comparator_51_eq, comparator_52_eq, comparator_54_eq, comparator_55_eq,
       comparator_56_eq, comparator_57_eq, comparator_58_eq, comparator_59_eq, comparator_60_eq,
       comparator_61_eq, comparator_62_eq, comparator_65_eq, comparator_66_eq, ImmSel_SB, ImmSel_U,
       ImmSel_UJ, isDivu, isMul, isMulh, isRemu, isSra, isSub, not_1_out, not_2_out, or_2_out, or_3_out,
       or_4_out, or_9_out, WBSel_ALUout, WBSel_Imm, WBSel_PC4;
  wire [1:0] multiplexer_13_out, multiplexer_14_out;
  wire [2:0] multiplexer_9_out, multiplexer_10_out, multiplexer_11_out;
  wire [3:0] multiplexer_1_out, multiplexer_2_out, multiplexer_3_out, multiplexer_4_out, multiplexer_5_out,
       multiplexer_6_out, RIsel;

  Comparator #(.width(7)) comparator_1 (.a(inst[31:25]), .b(7'b0000001), .eq(comparator_1_eq));  // open: gt, lt
  Comparator #(.width(3)) comparator_2 (.a(inst[14:12]), .b(3'b000), .eq(comparator_2_eq));  // open: gt, lt
  Comparator #(.width(7)) comparator_3 (.a(inst[6:0]), .b(7'b0110011), .eq(comparator_3_eq));  // open: gt, lt
  Comparator #(.width(7)) comparator_4 (.a(inst[31:25]), .b(7'b0100000), .eq(comparator_4_eq));  // open: gt, lt
  Comparator #(.width(3)) comparator_5 (.a(inst[14:12]), .b(3'b000), .eq(comparator_5_eq));  // open: gt, lt
  Comparator #(.width(7)) comparator_6 (.a(inst[6:0]), .b(7'b0110011), .eq(comparator_6_eq));  // open: gt, lt
  Comparator #(.width(7)) comparator_7 (.a(inst[31:25]), .b(7'b0000001), .eq(comparator_7_eq));  // open: gt, lt
  Comparator #(.width(3)) comparator_8 (.a(inst[14:12]), .b(3'b001), .eq(comparator_8_eq));  // open: gt, lt
  Comparator #(.width(7)) comparator_9 (.a(inst[6:0]), .b(7'b0110011), .eq(comparator_9_eq));  // open: gt, lt
  Comparator #(.width(7)) comparator_10 (.a(inst[31:25]), .b(7'b0100000), .eq(comparator_10_eq));  // open: gt, lt
  Comparator #(.width(3)) comparator_11 (.a(inst[14:12]), .b(3'b101), .eq(comparator_11_eq));  // open: gt, lt
  Comparator #(.width(7)) comparator_12 (.a(inst[6:0]), .b(7'b1100011), .eq(comparator_12_eq));  // open: gt, lt
  Comparator #(.width(3)) comparator_13 (.a(inst[14:12]), .b(3'b000), .eq(comparator_13_eq));  // open: gt, lt
  Comparator #(.width(3)) comparator_14 (.a(inst[14:12]), .b(3'b001), .eq(comparator_14_eq));  // open: gt, lt
  Comparator #(.width(3)) comparator_15 (.a(inst[14:12]), .b(3'b100), .eq(comparator_15_eq));  // open: gt, lt
  Comparator #(.width(3)) comparator_16 (.a(inst[14:12]), .b(3'b110), .eq(comparator_16_eq));  // open: gt, lt
  Comparator #(.width(3)) comparator_17 (.a(inst[14:12]), .b(3'b101), .eq(comparator_17_eq));  // open: gt, lt
  Comparator #(.width(3)) comparator_18 (.a(inst[14:12]), .b(3'b111), .eq(comparator_18_eq));  // open: gt, lt
  and and_1 (isMul, comparator_1_eq, comparator_2_eq, comparator_3_eq);
  and and_2 (isSub, comparator_4_eq, comparator_5_eq, comparator_6_eq);
  and and_3 (isMulh, comparator_7_eq, comparator_8_eq, comparator_9_eq);
  and and_4 (isSra, comparator_10_eq, comparator_11_eq);
  not not_1 (not_1_out, BrEq);
  not not_2 (not_2_out, BrLt);
  Comparator #(.width(7)) comparator_19 (.a(inst[6:0]), .b(7'b1101111), .eq(comparator_19_eq));  // open: gt, lt
  Comparator #(.width(7)) comparator_20 (.a(inst[6:0]), .b(7'b1100111), .eq(comparator_20_eq));  // open: gt, lt
  Multiplexer #(.select(3), .width(4), .enable("false")) multiplexer_1 (
    .in0(4'b0000), .in1(4'b0110), .in2(4'b0111), .in3(4'b1011), .in4(4'b0011), .in5(4'b0100), .in6(4'b0010),
    .in7(4'b0001), .out(multiplexer_1_out), .sel(inst[14:12]));
  and and_5 (and_5_out, comparator_12_eq, comparator_13_eq, BrEq);
  and and_6 (and_6_out, comparator_12_eq, comparator_14_eq, not_1_out);
  and and_7 (and_7_out, comparator_12_eq, comparator_15_eq, BrLt);
  and and_8 (and_8_out, comparator_12_eq, comparator_16_eq, BrLt);
  and and_9 (and_9_out, comparator_12_eq, comparator_17_eq, not_2_out);
  and and_10 (and_10_out, comparator_12_eq, comparator_18_eq, not_2_out);
  Multiplexer #(.width(4), .enable("false")) multiplexer_2 (
    .in0(multiplexer_1_out), .in1(4'b1010), .out(multiplexer_2_out), .sel(isMul));
  Comparator #(.width(7)) comparator_21 (.a(inst[6:0]), .b(7'b1101111), .eq(comparator_21_eq));  // open: gt, lt
  Comparator #(.width(7)) comparator_22 (.a(inst[6:0]), .b(7'b0110111), .eq(comparator_22_eq));  // open: gt, lt
  Comparator #(.width(7)) comparator_23 (.a(inst[6:0]), .b(7'b0010111), .eq(comparator_23_eq));  // open: gt, lt
  Comparator #(.width(7)) comparator_24 (.a(inst[6:0]), .b(7'b1100111), .eq(comparator_24_eq));  // open: gt, lt
  Comparator #(.width(7)) comparator_25 (.a(inst[6:0]), .b(7'b0110011), .eq(comparator_25_eq));  // open: gt, lt
  Comparator #(.width(7)) comparator_26 (.a(inst[6:0]), .b(7'b0010011), .eq(comparator_26_eq));  // open: gt, lt
  Comparator #(.width(7)) comparator_27 (.a(inst[6:0]), .b(7'b0000011), .eq(comparator_27_eq));  // open: gt, lt
  Multiplexer #(.width(4), .enable("false")) multiplexer_3 (
    .in0(multiplexer_2_out), .in1(4'b1100), .out(multiplexer_3_out), .sel(isSub));
  Multiplexer #(.width(4), .enable("false")) multiplexer_4 (
    .in0(multiplexer_3_out), .in1(4'b1110), .out(multiplexer_4_out), .sel(isMulh));
  Comparator #(.width(7)) comparator_28 (.a(inst[6:0]), .b(7'b1101111), .eq(comparator_28_eq));  // open: gt, lt
  Comparator #(.width(7)) comparator_29 (.a(inst[6:0]), .b(7'b0010111), .eq(comparator_29_eq));  // open: gt, lt
  or or_1 (PCSel, and_5_out, and_6_out, and_7_out, and_8_out, and_9_out, and_10_out, comparator_19_eq, comparator_20_eq);
  Multiplexer #(.width(4), .enable("false")) multiplexer_5 (
    .in0(multiplexer_4_out), .in1(4'b0101), .out(multiplexer_5_out), .sel(isSra));
  or or_2 (or_2_out, comparator_30_eq, comparator_31_eq);
  Comparator #(.width(7)) comparator_30 (.a(inst[6:0]), .b(7'b0110011), .eq(comparator_30_eq));  // open: gt, lt
  Comparator #(.width(7)) comparator_31 (.a(inst[6:0]), .b(7'b0010011), .eq(comparator_31_eq));  // open: gt, lt
  Comparator #(.width(7)) comparator_32 (.a(inst[31:25]), .b(7'b0000001), .eq(comparator_32_eq));  // open: gt, lt
  Comparator #(.width(3)) comparator_33 (.a(inst[14:12]), .b(3'b101), .eq(comparator_33_eq));  // open: gt, lt
  Comparator #(.width(7)) comparator_34 (.a(inst[6:0]), .b(7'b0110011), .eq(comparator_34_eq));  // open: gt, lt
  Comparator #(.width(7)) comparator_35 (.a(inst[31:25]), .b(7'b0000001), .eq(comparator_35_eq));  // open: gt, lt
  Comparator #(.width(3)) comparator_36 (.a(inst[14:12]), .b(3'b111), .eq(comparator_36_eq));  // open: gt, lt
  Comparator #(.width(7)) comparator_37 (.a(inst[6:0]), .b(7'b0110011), .eq(comparator_37_eq));  // open: gt, lt
  or or_3 (or_3_out, comparator_21_eq, comparator_22_eq, comparator_23_eq);
  or or_4 (or_4_out, comparator_25_eq, comparator_26_eq, comparator_27_eq);
  or or_5 (ASel, comparator_28_eq, comparator_12_eq, comparator_29_eq);
  Multiplexer #(.width(4), .enable("false")) multiplexer_6 (
    .in0(multiplexer_5_out), .in1(4'b1000), .out(multiplexer_6_out), .sel(isDivu));
  Multiplexer #(.width(4), .enable("false")) multiplexer_7 (.in0(4'b0000), .in1(RIsel), .out(ALUSel), .sel(or_2_out));
  and and_11 (isDivu, comparator_32_eq, comparator_33_eq, comparator_34_eq);
  and and_12 (isRemu, comparator_35_eq, comparator_36_eq, comparator_37_eq);
  or or_6 (RegWEn, or_3_out, comparator_24_eq, or_4_out);
  Multiplexer #(.width(4), .enable("false")) multiplexer_8 (
    .in0(multiplexer_6_out), .in1(4'b1001), .out(RIsel), .sel(isRemu));
  Comparator #(.width(7)) comparator_38 (.a(inst[6:0]), .b(7'b0010111), .eq(comparator_38_eq));  // open: gt, lt
  Comparator #(.width(7)) comparator_39 (.a(inst[6:0]), .b(7'b0110011), .eq(comparator_39_eq));  // open: gt, lt
  Comparator #(.width(7)) comparator_40 (.a(inst[6:0]), .b(7'b0010011), .eq(comparator_40_eq));  // open: gt, lt
  Comparator #(.width(7)) comparator_41 (.a(inst[6:0]), .b(7'b1100111), .eq(comparator_41_eq));  // open: gt, lt
  Comparator #(.width(7)) comparator_42 (.a(inst[6:0]), .b(7'b1101111), .eq(comparator_42_eq));  // open: gt, lt
  Comparator #(.width(3)) comparator_43 (.a(inst[14:12]), .b(3'b110), .eq(comparator_43_eq));  // open: gt, lt
  Comparator #(.width(3)) comparator_44 (.a(inst[14:12]), .b(3'b111), .eq(comparator_44_eq));  // open: gt, lt
  Multiplexer #(.width(3), .enable("false")) multiplexer_9 (
    .in0(3'b000), .in1(3'b001), .out(multiplexer_9_out), .sel(MemRW));
  or or_7 (WBSel_ALUout, comparator_38_eq, comparator_39_eq, comparator_40_eq);
  Comparator #(.width(7)) comparator_45 (.a(inst[6:0]), .b(7'b0110111), .eq(WBSel_Imm));  // open: gt, lt
  Comparator #(.width(7)) comparator_46 (.a(inst[6:0]), .b(7'b0010011), .eq(comparator_46_eq));  // open: gt, lt
  Comparator #(.width(7)) comparator_47 (.a(inst[6:0]), .b(7'b0000011), .eq(comparator_47_eq));  // open: gt, lt
  Comparator #(.width(7)) comparator_48 (.a(inst[6:0]), .b(7'b1100011), .eq(comparator_48_eq));  // open: gt, lt
  Comparator #(.width(7)) comparator_49 (.a(inst[6:0]), .b(7'b1100111), .eq(comparator_49_eq));  // open: gt, lt
  Comparator #(.width(7)) comparator_50 (.a(inst[6:0]), .b(7'b0010111), .eq(comparator_50_eq));  // open: gt, lt
  Comparator #(.width(7)) comparator_51 (.a(inst[6:0]), .b(7'b0110111), .eq(comparator_51_eq));  // open: gt, lt
  Comparator #(.width(7)) comparator_52 (.a(inst[6:0]), .b(7'b1101111), .eq(comparator_52_eq));  // open: gt, lt
  Comparator #(.width(7)) comparator_53 (.a(inst[6:0]), .b(7'b1101111), .eq(ImmSel_UJ));  // open: gt, lt
  Multiplexer #(.width(3), .enable("false")) multiplexer_10 (
    .in0(multiplexer_9_out), .in1(3'b010), .out(multiplexer_10_out), .sel(ImmSel_SB));
  Comparator #(.width(7)) comparator_54 (.a(inst[6:0]), .b(7'b0010011), .eq(comparator_54_eq));  // open: gt, lt
  Comparator #(.width(7)) comparator_55 (.a(inst[6:0]), .b(7'b0000011), .eq(comparator_55_eq));  // open: gt, lt
  Comparator #(.width(7)) comparator_56 (.a(inst[6:0]), .b(7'b1100011), .eq(comparator_56_eq));  // open: gt, lt
  Comparator #(.width(7)) comparator_57 (.a(inst[6:0]), .b(7'b1100111), .eq(comparator_57_eq));  // open: gt, lt
  Comparator #(.width(7)) comparator_58 (.a(inst[6:0]), .b(7'b0010111), .eq(comparator_58_eq));  // open: gt, lt
  Comparator #(.width(7)) comparator_59 (.a(inst[6:0]), .b(7'b0110111), .eq(comparator_59_eq));  // open: gt, lt
  Comparator #(.width(7)) comparator_60 (.a(inst[6:0]), .b(7'b1101111), .eq(comparator_60_eq));  // open: gt, lt
  or or_8 (WBSel_PC4, comparator_41_eq, comparator_42_eq);
  Comparator #(.width(7)) comparator_61 (.a(inst[6:0]), .b(7'b0010111), .eq(comparator_61_eq));  // open: gt, lt
  Comparator #(.width(7)) comparator_62 (.a(inst[6:0]), .b(7'b0110111), .eq(comparator_62_eq));  // open: gt, lt
  Comparator #(.width(7)) comparator_63 (.a(inst[6:0]), .b(7'b0100011), .eq(MemRW));  // open: gt, lt
  Comparator #(.width(7)) comparator_64 (.a(inst[6:0]), .b(7'b1100011), .eq(ImmSel_SB));  // open: gt, lt
  or or_9 (or_9_out, comparator_43_eq, comparator_44_eq);
  Multiplexer #(.width(3), .enable("false")) multiplexer_11 (
    .in0(multiplexer_10_out), .in1(3'b011), .out(multiplexer_11_out), .sel(ImmSel_U));
  and and_13 (BrUn, ImmSel_SB, or_9_out);
  or or_10 (ImmSel_U, comparator_61_eq, comparator_62_eq);
  Multiplexer #(.width(3), .enable("false")) multiplexer_12 (
    .in0(multiplexer_11_out), .in1(3'b100), .out(ImmSel), .sel(ImmSel_UJ));
  or or_11 (BSel, comparator_65_eq, comparator_54_eq, comparator_55_eq, comparator_56_eq, comparator_58_eq, comparator_59_eq, comparator_60_eq, comparator_57_eq);
  or or_12 (BSel, comparator_66_eq, comparator_46_eq, comparator_47_eq, comparator_48_eq, comparator_50_eq, comparator_51_eq, comparator_52_eq, comparator_49_eq);
  Comparator #(.width(7)) comparator_65 (.a(inst[6:0]), .b(7'b0100011), .eq(comparator_65_eq));  // open: gt, lt
  Multiplexer #(.width(2), .enable("false")) multiplexer_13 (
    .in0(2'b00), .in1(2'b01), .out(multiplexer_13_out), .sel(WBSel_ALUout));
  Comparator #(.width(7)) comparator_66 (.a(inst[6:0]), .b(7'b0100011), .eq(comparator_66_eq));  // open: gt, lt
  Multiplexer #(.width(2), .enable("false")) multiplexer_14 (
    .in0(multiplexer_13_out), .in1(2'b10), .out(multiplexer_14_out), .sel(WBSel_PC4));
  Multiplexer #(.width(2), .enable("false")) multiplexer_15 (
    .in0(multiplexer_14_out), .in1(2'b11), .out(WBSel), .sel(WBSel_Imm));

  // Other names for the same wires on the sheet: ImmSel_S = MemRW; opcode[6:0] = inst[6:0]; rd[4:0] = inst[11:7];
  //   func3[2:0] = inst[14:12]; rs1[4:0] = inst[19:15]; rs2[4:0] = inst[24:20]; func7[6:0] = inst[31:25]

  // Notes on the sheet:
  //   deal with R type
  //   INPUTS to your circuit
  //   特判特定指令
  //   beq
  //   bne
  //   blt
  //   bltu
  //   bge
  //   bgeu
  //   是分支指令
  //   jal指令
  //   jalr指令
  //   处理ALUSel
  //   DON'T CHANGE THE LOCATIONS OF THE INPUTS AND OUTPUTS!
  //   OUTPUT from your circuit
  //   jal
  //   lui
  //   auipc
  //   jalr
  //   R
  //   I
  //   load
  //   左边MUX根据i型指令或者R型指令选择相应的计算方式（因为这一部分指令I型和R型指令只要是相同的类型就会有相同的func3）
  //   R指令
  //   I指令
  //   处理RegWEn，凡是需要写回rd的都算进来
  //   除了R和I type计算指令，其余指令都默认加法
  //   处理Asel和PCSel
  //   R
  //   I
  //   jal指令写回pc + 4
  //   lui指令写回立即数
  //   处理immsel
  //   BSel.直接看哪些指令需要立即数即可
  //   处理WBSel
  //   选择立即数还是寄存器的BSel
endmodule
