// Logisim project cpu.circ as structural Verilog: 1 circuit, main circuit main
module main (
  input  [31:0] INSTRUCTION,
  input  CLOCK,
  output [31:0] PROGRAM_COUNTER,
  output [31:0] ra,
  output [31:0] sp,
  output [31:0] t0,
  output [31:0] t1,
  output [31:0] t2,
  output [31:0] s0,
  output [31:0] s1,
  output [31:0] a0
);

  wire ASel, BrEq, BrLt, BrUn, BSel, MemRW, PCSel, RegWEn, undriven;
  wire [1:0] WBSel;
  wire [2:0] func3, ImmSel;
  wire [3:0] ALUSel;
  wire [6:0] func7;
  wire [24:0] instruction_fetched;
  wire [31:0] adder_1_out, alu_out, imm, mem_data, multiplexer_1_out, multiplexer_2_out, multiplexer_3_out,
       multiplexer_4_out, PC4, PROGRAM_COUNTER2, rs1value, rs2value, wb;

  control_logic control_logic_1 (
    .BSel(BSel), .BrUn(BrUn), .RegWEn(RegWEn), .ImmSel(ImmSel), .ASel(ASel), .PCSel(PCSel), .BrLt(BrLt),
    .BrEq(BrEq), .inst({func7, instruction_fetched[24:15], func3, instruction_fetched[11:0]}),
    .ALUSel(ALUSel), .MemRW(MemRW), .WBSel(WBSel));
  Adder #(.width(32)) adder_1 (.a(PROGRAM_COUNTER), .b(32'h4), .out(adder_1_out));  // open: cin, cout
  Register #(.width(32)) PC (.D(multiplexer_1_out), .clk(CLOCK), .Q(PROGRAM_COUNTER));  // open: en, clr
  Multiplexer #(.width(32), .enable("false")) multiplexer_1 (
    .in0(adder_1_out), .in1(alu_out), .out(multiplexer_1_out), .sel(PCSel));
  imm_gen imm_gen_1 (
    .ImmSel(ImmSel), .imm(imm), .inst({func7, instruction_fetched[24:15], func3, instruction_fetched[11:0]}));
  Register #(.width(32)) register_1 (.D(PROGRAM_COUNTER), .clk(CLOCK), .Q(PROGRAM_COUNTER2));  // open: en, clr
  Adder #(.width(32)) adder_2 (.a(PROGRAM_COUNTER2), .b(32'h4), .out(PC4));  // open: cin, cout
  Multiplexer #(.width(32), .enable("false")) multiplexer_2 (
    .in0(INSTRUCTION), .in1(32'h13), .out(multiplexer_2_out), .sel(PCSel));
  Register #(.width(32)) register_2 (
    .D(multiplexer_2_out), .clk(CLOCK),
    .Q({func7, instruction_fetched[24:15], func3, instruction_fetched[11:0]}), .clr(undriven));  // open: en
  regfile_main RegFile (
    .rs2(instruction_fetched[24:20]), .rd(instruction_fetched[11:7]), .Read_Data_1(rs1value),
    .Read_Data_2(rs2value), .ra(ra), .sp(sp), .t0(t0), .t1(t1), .t2(t2), .s0(s0), .s1(s1), .a0(a0),
    .rs1(instruction_fetched[19:15]), .Write_Data(wb), .RegWEn(RegWEn), .clk(CLOCK));
  branch_comp branch_comp_1 (.BrEq(BrEq), .BrUn(BrUn), .rs1(rs1value), .BrLt(BrLt), .rs2(rs2value));
  Multiplexer #(.width(32), .enable("false")) multiplexer_3 (
    .in0(rs1value), .in1(PROGRAM_COUNTER2), .out(multiplexer_3_out), .sel(ASel));
  Multiplexer #(.width(32), .enable("false")) multiplexer_4 (
    .in0(rs2value), .in1(imm), .out(multiplexer_4_out), .sel(BSel));
  alu Arithmetic_Logic_Unit (.ALUSel(ALUSel), .Result(alu_out), .A(multiplexer_3_out), .B(multiplexer_4_out));
  // mem_main DMEM: pin names not known; wires that end beside it: alu_out, rs2value, CLOCK, MemRW, mem_data
  Multiplexer #(.select(2), .width(32), .enable("false")) multiplexer_5 (
    .in0(mem_data), .in1(alu_out), .in2(PC4), .in3(imm), .out(wb), .sel(WBSel));

  // Other names for the same wires on the sheet: clk = CLOCK; opcode[6:0] = instruction_fetched[6:0];
  //   rd[4:0] = instruction_fetched[11:7]; instruction_fetched (some bits) = {func7, func3};
  //   rs1[4:0] = instruction_fetched[19:15]; rs2[4:0] = instruction_fetched[24:20]

  // Notes on the sheet:
  //   decode
  //   Output
  //   IMEM (do **NOT** move this)
  //   Inputs
  //   在这里处理control hazzard，如果PCSel了，说明遇到了条件跳转指令和分支指令满足条件，需要添加nop指令
  //   It is OK to move the PC, RegFile, ALU, MEM, Branch Comp, Imm Gen, and Control Logic to wherever is most convenient for you when constructing your CPU, and to delete this text
  //   Inputs/Outputs for testing. Do **NOT** move these.
endmodule
